# Fritzing sketch test-push-button (saved by Fritzing 0.9.4)
breadboards: 1

parts:
  元件1 = Arduino Uno (Rev3)
  S1 = Pushbutton [package="[THT]"]
  R1 = Resistor [tolerance=±5% resistance=220 package=THT]

nets:
  N1: 元件1.GND, S1.Pin_1, S1.Pin_2
  N2: 元件1.D2, S1.Pin_3, S1.Pin_4, R1.Pin_1
  N3: 元件1.5V, R1.Pin_0
